// Digital circuit CPU_RISCV.dig as structural Verilog
module CPU_RISCV (
  input  [31:0] A,
  input  [31:0] B,
  input  [3:0] ALUControl,
  output [31:0] Result,
  output Zero
);

  ALU_32 #(.applicationType("IVERILOG"), .CodeFile("/Users/kellysoares/Documents/Faculdade/arqComp/RICV_entrega/ALU_32.v")) u_ALU_32 (
    .A(A), .B(B), .ALUControl(ALUControl), .Result(Result), .Zero(Zero));
endmodule
